// Logisim project 实验1.circ as structural Verilog: 5 circuits, main circuit 一位二进制半加器
module \一位二进制半加器  (
  input  A,
  input  B,
  output S,
  output C
);

  wire and_2_out, and_3_out, not_1_out, not_2_out;

  not not_1 (not_1_out, A);
  not not_2 (not_2_out, B);
  and and_1 (C, A, B);
  and and_2 (and_2_out, not_1_out, B);
  and and_3 (and_3_out, A, not_2_out);
  or or_1 (S, and_2_out, and_3_out);
endmodule

module \一位二进制全加器  (
  input  Ci,
  input  A,
  input  B,
  output S,
  output Co
);

  wire and_1_out, and_2_out, and_3_out, and_4_out, and_5_out, and_6_out, and_7_out, not_1_out, not_2_out,
       not_3_out, not_4_out, not_5_out, not_6_out;

  not not_1 (not_1_out, Ci);
  not not_2 (not_2_out, A);
  not not_3 (not_3_out, Ci);
  not not_4 (not_4_out, B);
  not not_5 (not_5_out, A);
  not not_6 (not_6_out, B);
  and and_1 (and_1_out, A, B);
  and and_2 (and_2_out, Ci, B);
  and and_3 (and_3_out, Ci, A);
  and and_4 (and_4_out, not_1_out, not_2_out, B);
  and and_5 (and_5_out, not_3_out, A, not_4_out);
  and and_6 (and_6_out, Ci, not_5_out, not_6_out);
  and and_7 (and_7_out, Ci, A, B);
  or or_1 (Co, and_1_out, and_2_out, and_3_out);
  or or_2 (S, and_4_out, and_5_out, and_6_out, and_7_out);
endmodule

// 四位二进制并行加法器
module \先行进位并行加法器  (
  input  A3,
  input  B3,
  input  A2,
  input  B2,
  input  A1,
  input  B1,
  input  A0,
  input  B0,
  input  C0,
  output C4,
  output S3,
  output S2,
  output S1,
  output S0
);

  wire and_1_out, and_2_out, and_3_out, and_4_out, and_5_out, and_6_out, and_7_out, and_8_out, or_1_out,
       or_2_out, or_3_out, xor_1_out, xor_3_out, xor_5_out, xor_7_out;

  and and_1 (and_1_out, A0, B0);
  and and_2 (and_2_out, xor_1_out, C0);
  xor xor_1 (xor_1_out, A0, B0);
  or or_1 (or_1_out, and_1_out, and_2_out);
  xor xor_2 (S0, xor_1_out, C0);
  and and_3 (and_3_out, A1, B1);
  xor xor_3 (xor_3_out, A1, B1);
  and and_4 (and_4_out, xor_3_out, or_1_out);
  or or_2 (or_2_out, and_3_out, and_4_out);
  xor xor_4 (S1, xor_3_out, or_1_out);
  and and_5 (and_5_out, A2, B2);
  xor xor_5 (xor_5_out, A2, B2);
  and and_6 (and_6_out, xor_5_out, or_2_out);
  xor xor_6 (S2, xor_5_out, or_2_out);
  or or_3 (or_3_out, and_5_out, and_6_out);
  xor xor_7 (xor_7_out, A3, B3);
  and and_7 (and_7_out, A3, B3);
  or or_4 (C4, and_7_out, and_8_out);
  and and_8 (and_8_out, xor_7_out, or_3_out);
  xor xor_8 (S3, xor_7_out, or_3_out);
endmodule

module \先行进位并行加法器测试电路  (
  input  in_1,
  input  in_2,
  input  in_3,
  input  in_4,
  input  in_5,
  input  in_6,
  input  in_7,
  input  in_8,
  input  in_9,
  output out_10,
  output out_11,
  output out_12,
  output out_13,
  output out_14
);

  \先行进位并行加法器  \u_先行进位并行加法器_1  (
    .A3(in_2), .B3(in_3), .A2(in_4), .B2(in_5), .A1(in_6), .B1(in_7), .A0(in_8), .B0(in_9), .C0(in_1),
    .C4(out_14), .S3(out_10), .S2(out_11), .S1(out_12), .S0(out_13));
endmodule

module \串行进位并行加法器  (
  input  C0,
  input  A0,
  input  B0,
  input  A1,
  input  A2,
  input  A3,
  input  B1,
  input  B2,
  input  B3,
  output S0,
  output S1,
  output S2,
  output S3,
  output C4
);

  wire \一位二进制全加器_1_co , \一位二进制全加器_2_co , \一位二进制全加器_3_co ;

  \一位二进制全加器  \u_一位二进制全加器_1  (.Ci(C0), .A(A0), .B(B0), .S(S0), .Co(\一位二进制全加器_1_co ));
  \一位二进制全加器  \u_一位二进制全加器_2  (.Ci(\一位二进制全加器_1_co ), .A(A1), .B(B1), .S(S1), .Co(\一位二进制全加器_2_co ));
  \一位二进制全加器  \u_一位二进制全加器_3  (.Ci(\一位二进制全加器_2_co ), .A(A2), .B(B2), .S(S2), .Co(\一位二进制全加器_3_co ));
  \一位二进制全加器  \u_一位二进制全加器_4  (.Ci(\一位二进制全加器_3_co ), .A(A3), .B(B3), .S(S3), .Co(C4));
endmodule
