// Logisim project 实验2.circ as structural Verilog: 9 circuits, main circuit 四位二进制可逆计数器
module \四位二进制可逆计数器  (
  input  A,
  input  CPd,
  input  CPu,
  input  B,
  input  C,
  input  D,
  input  CLR,
  input  LD,
  output Qa,
  output Qb,
  output Qc,
  output Qd
);

  wire and_1_out, and_2_out, and_3_out, and_4_out, and_5_out, and_6_out, d_ff_1_qn, d_ff_2_qn, d_ff_3_qn,
       d_ff_4_qn, nand_1_out, nand_2_out, nand_3_out, nand_4_out, nand_5_out, nand_6_out, nand_7_out,
       nand_8_out, not_1_out, not_2_out, not_3_out, not_4_out, not_5_out, not_6_out, not_7_out, not_8_out,
       not_9_out, not_10_out, not_11_out, not_12_out, not_13_out, not_14_out, not_15_out, not_16_out,
       not_17_out, not_18_out, not_19_out, not_20_out, or_1_out, or_2_out, or_3_out, or_4_out, or_5_out,
       or_6_out, or_7_out, or_8_out;

  not not_1 (not_1_out, CPd);
  not not_2 (not_2_out, CPu);
  not not_3 (not_3_out, CLR);
  not not_4 (not_4_out, LD);
  and and_1 (and_1_out, not_1_out, d_ff_1_qn);
  and and_2 (and_2_out, Qa, not_2_out);
  and and_3 (and_3_out, not_1_out, d_ff_1_qn, d_ff_2_qn);
  and and_4 (and_4_out, Qa, Qb, not_2_out);
  and and_5 (and_5_out, not_1_out, d_ff_1_qn, d_ff_2_qn, d_ff_3_qn);
  and and_6 (and_6_out, Qa, Qb, Qc, not_2_out);
  nand nand_1 (nand_1_out, A, not_4_out, not_3_out);
  or or_1 (or_1_out, not_1_out, not_2_out);
  nand nand_2 (nand_2_out, B, not_4_out, not_3_out);
  or or_2 (or_2_out, and_1_out, and_2_out);
  nand nand_3 (nand_3_out, C, not_4_out, not_3_out);
  or or_3 (or_3_out, and_3_out, and_4_out);
  nand nand_4 (nand_4_out, D, not_4_out, not_3_out);
  or or_4 (or_4_out, and_5_out, and_6_out);
  nand nand_5 (nand_5_out, nand_1_out, not_4_out);
  nand nand_6 (nand_6_out, nand_2_out, not_4_out);
  nand nand_7 (nand_7_out, nand_3_out, not_4_out);
  nand nand_8 (nand_8_out, nand_4_out, not_4_out);
  not not_5 (not_5_out, nand_1_out);
  not not_6 (not_6_out, not_3_out);
  or or_5 (or_5_out, not_6_out, not_7_out);
  not not_7 (not_7_out, nand_5_out);
  not not_8 (not_8_out, nand_2_out);
  not not_9 (not_9_out, or_2_out);
  not not_10 (not_10_out, not_3_out);
  or or_6 (or_6_out, not_10_out, not_11_out);
  not not_11 (not_11_out, nand_6_out);
  not not_12 (not_12_out, nand_3_out);
  not not_13 (not_13_out, or_3_out);
  not not_14 (not_14_out, not_3_out);
  or or_7 (or_7_out, not_14_out, not_15_out);
  not not_15 (not_15_out, nand_7_out);
  not not_16 (not_16_out, nand_4_out);
  not not_17 (not_17_out, or_4_out);
  not not_18 (not_18_out, not_3_out);
  or or_8 (or_8_out, not_18_out, not_19_out);
  not not_19 (not_19_out, nand_8_out);
  D_Flip_Flop #(.trigger("rising"), .Pre_Clr_Positions("ABOVE_BELOW"), .NegatePresetClear("false"), .enable("false"), .NewFFLayout("true")) d_ff_1 (
    .clk(not_20_out), .D(d_ff_1_qn), .Q(Qa), .Qn(d_ff_1_qn), .preset(not_5_out), .reset(or_5_out));
  not not_20 (not_20_out, or_1_out);
  D_Flip_Flop #(.trigger("rising"), .Pre_Clr_Positions("ABOVE_BELOW"), .NegatePresetClear("false"), .enable("false"), .NewFFLayout("true")) d_ff_2 (
    .clk(not_9_out), .D(d_ff_2_qn), .Q(Qb), .Qn(d_ff_2_qn), .preset(not_8_out), .reset(or_6_out));
  D_Flip_Flop #(.trigger("rising"), .Pre_Clr_Positions("ABOVE_BELOW"), .NegatePresetClear("false"), .enable("false"), .NewFFLayout("true")) d_ff_3 (
    .clk(not_13_out), .D(d_ff_3_qn), .Q(Qc), .Qn(d_ff_3_qn), .preset(not_12_out), .reset(or_7_out));
  D_Flip_Flop #(.trigger("rising"), .Pre_Clr_Positions("ABOVE_BELOW"), .NegatePresetClear("false"), .enable("false"), .NewFFLayout("true")) d_ff_4 (
    .clk(not_17_out), .D(d_ff_4_qn), .Q(Qd), .Qn(d_ff_4_qn), .preset(not_16_out), .reset(or_8_out));
endmodule

module \四位二进制可逆计数器测试电路  (
  input  in_1,
  input  in_2,
  input  in_3,
  input  in_4,
  input  in_5,
  input  in_6,
  input  in_7,
  input  in_8,
  output out_9,
  output out_10,
  output out_11,
  output out_12
);

  \四位二进制可逆计数器  \u_四位二进制可逆计数器_1  (
    .A(in_8), .CPd(in_3), .CPu(in_1), .B(in_7), .C(in_5), .D(in_4), .CLR(in_2), .LD(in_6), .Qa(out_12),
    .Qb(out_11), .Qc(out_10), .Qd(out_9));
endmodule

module \二进制转8421码电路  (
  input  D,
  input  C,
  input  B,
  input  A,
  output S8,
  output S4,
  output S2,
  output S1,
  output S20,
  output S40,
  output S80,
  output S10
);

  wire and_1_out, or_1_out;

  and and_1 (and_1_out, D, or_1_out);
  // 先行进位并行加法器 先行进位并行加法器_1: pin names not known; wires that end beside it: 1'b0, 1'b0, S8, and_1_out, and_1_out, S4, 1'b0, S2, D, C, S1, B, A, S10
  or or_1 (or_1_out, B, C);

  assign S20 = 1'b0;
  assign S40 = 1'b0;
  assign S80 = 1'b0;
endmodule

module \二进制转8421码测试电路  (
  input  in_1,
  input  in_2,
  input  in_3,
  input  in_4,
  output out_5,
  output out_6,
  output out_7,
  output out_8,
  output out_9,
  output out_10,
  output out_11,
  output out_12
);

  \二进制转8421码电路  \u_二进制转8421码电路_1  (
    .S20(out_7), .S40(out_6), .S80(out_5), .S10(out_8), .S8(out_9), .S4(out_10), .S2(out_11), .S1(out_12),
    .D(in_1), .C(in_2), .B(in_3), .A(in_4));
endmodule

module \显示电路  (
  input  A3,
  input  A2,
  input  A1,
  input  A0,
  output a,
  output b,
  output c,
  output d,
  output e,
  output f,
  output g
);

  wire and_1_out, and_2_out, and_3_out, and_4_out, and_5_out, and_6_out, and_7_out, and_8_out, and_9_out,
       and_10_out, and_11_out, and_12_out, and_13_out, and_14_out, and_15_out, and_16_out, and_17_out,
       and_18_out, and_19_out, and_20_out, and_21_out, and_22_out, and_23_out, and_24_out, and_25_out,
       and_26_out, not_1_out, not_2_out, not_3_out, not_4_out, not_5_out, not_6_out, not_7_out, not_8_out,
       not_9_out, not_10_out, not_11_out, not_12_out, not_13_out, not_14_out, not_15_out, not_16_out,
       not_17_out, not_18_out, not_19_out, not_20_out, not_21_out, not_22_out, not_23_out, not_24_out,
       not_25_out, not_26_out, not_27_out, not_28_out, not_29_out, not_30_out, not_31_out, not_32_out,
       not_33_out, not_34_out, not_35_out, not_36_out, not_37_out;

  not not_1 (not_1_out, A3);
  and and_1 (and_1_out, not_1_out, not_2_out, not_3_out);
  not not_2 (not_2_out, A2);
  not not_3 (not_3_out, A0);
  not not_4 (not_4_out, A3);
  and and_2 (and_2_out, not_4_out, not_5_out, A1);
  not not_5 (not_5_out, A2);
  not not_6 (not_6_out, A3);
  and and_3 (and_3_out, not_6_out, A2, A0);
  and and_4 (and_4_out, A3, not_7_out, not_8_out);
  not not_7 (not_7_out, A2);
  not not_8 (not_8_out, A1);
  not not_9 (not_9_out, A1);
  and and_5 (and_5_out, A3, not_9_out, A0);
  not not_10 (not_10_out, A3);
  and and_6 (and_6_out, not_10_out, not_11_out);
  not not_11 (not_11_out, A2);
  not not_12 (not_12_out, A2);
  and and_7 (and_7_out, not_12_out, not_13_out);
  not not_13 (not_13_out, A1);
  not not_14 (not_14_out, A1);
  and and_8 (and_8_out, not_14_out, not_15_out);
  not not_15 (not_15_out, A0);
  not not_16 (not_16_out, A3);
  and and_9 (and_9_out, not_16_out, A1, A0);
  not not_17 (not_17_out, A2);
  and and_10 (and_10_out, not_17_out, not_18_out);
  not not_18 (not_18_out, A1);
  not not_19 (not_19_out, A2);
  and and_11 (and_11_out, not_19_out, A0);
  not not_20 (not_20_out, A3);
  and and_12 (and_12_out, not_20_out, A2);
  not not_21 (not_21_out, A2);
  and and_13 (and_13_out, not_21_out, not_22_out);
  not not_22 (not_22_out, A0);
  not not_23 (not_23_out, A2);
  and and_14 (and_14_out, not_23_out, A1);
  and and_15 (and_15_out, A1, not_24_out);
  not not_24 (not_24_out, A0);
  and and_16 (and_16_out, A2, not_25_out, A0);
  not not_25 (not_25_out, A1);
  not not_26 (not_26_out, A2);
  and and_17 (and_17_out, not_26_out, not_27_out);
  not not_27 (not_27_out, A0);
  and and_18 (and_18_out, A1, not_28_out);
  not not_28 (not_28_out, A0);
  not not_29 (not_29_out, A1);
  and and_19 (and_19_out, not_29_out, not_30_out);
  not not_30 (not_30_out, A0);
  and and_20 (and_20_out, A2, not_31_out);
  not not_31 (not_31_out, A1);
  and and_21 (and_21_out, A2, not_32_out);
  not not_32 (not_32_out, A0);
  and and_22 (and_22_out, A3, not_33_out);
  not not_33 (not_33_out, A1);
  not not_34 (not_34_out, A2);
  and and_23 (and_23_out, not_34_out, A1);
  and and_24 (and_24_out, A2, not_35_out);
  not not_35 (not_35_out, A1);
  and and_25 (and_25_out, A2, not_36_out);
  not not_36 (not_36_out, A0);
  and and_26 (and_26_out, A3, not_37_out);
  not not_37 (not_37_out, A2);
  or or_1 (a, and_1_out, and_2_out, and_3_out, and_4_out, and_5_out);
  or or_2 (b, and_6_out, and_7_out, and_8_out, and_9_out);
  or or_3 (c, and_10_out, and_11_out, and_12_out);
  or or_4 (d, and_13_out, and_14_out, and_15_out, and_16_out);
  or or_5 (e, and_17_out, and_18_out);
  or or_6 (f, and_19_out, and_20_out, and_21_out, and_22_out);
  or or_7 (g, and_23_out, and_24_out, and_25_out, and_26_out);
endmodule

module \显示电路测试电路  (
  input  in_1,
  input  in_2,
  input  in_3,
  input  in_4
);

  wire \显示电路_1_a , \显示电路_1_b , \显示电路_1_c , \显示电路_1_d , \显示电路_1_e , \显示电路_1_f , \显示电路_1_g ;

  _7_Segment_Display #(.active("true")) u_7_segment_display_1 (
    .g(\显示电路_1_g ), .f(\显示电路_1_f ), .a(\显示电路_1_a ), .b(\显示电路_1_b ), .e(\显示电路_1_e ), .d(\显示电路_1_d ),
    .c(\显示电路_1_c ));  // open: dp
  \显示电路  \u_显示电路_1  (
    .A3(in_1), .A2(in_2), .A1(in_3), .A0(in_4), .a(\显示电路_1_a ), .b(\显示电路_1_b ), .c(\显示电路_1_c ),
    .d(\显示电路_1_d ), .e(\显示电路_1_e ), .f(\显示电路_1_f ), .g(\显示电路_1_g ));
endmodule

module \报警电路  (
  input  CPu,
  input  CLR,
  input  CPd,
  input  in_4,
  input  in_5,
  input  in_6,
  input  in_7,
  input  in_8,
  output out_9,
  output out_10,
  output out_11,
  output out_12,
  output \报警 
);

  wire not_1_out, or_1_out, or_2_out, \无人_out , \满人_out ;

  LED #(.active("true")) led_1 (.in(\报警 ));
  and and_1 (\报警 , CPu, \满人_out );
  not not_1 (not_1_out, \无人_out );
  or \u_无人  (\无人_out , out_12, out_11, out_10, out_9);
  and \u_满人  (\满人_out , out_12, out_11, out_10, out_9);
  or or_1 (or_1_out, \满人_out , CPu);
  or or_2 (or_2_out, not_1_out, CPd);
  \四位二进制可逆计数器  \u_四位二进制可逆计数器_1  (
    .A(in_7), .CPd(or_2_out), .CPu(or_1_out), .B(in_6), .C(in_5), .D(in_4), .CLR(CLR), .LD(in_8),
    .Qa(out_12), .Qb(out_11), .Qc(out_10), .Qd(out_9));
endmodule

// 封禁后的门禁系统逻辑符号
module \小型实验室门禁系统  (
  input  CPu,
  input  CLR,
  input  CPd,
  output a1,
  output b1,
  output c1,
  output d1,
  output e1,
  output f1,
  output g1,
  output a0,
  output b0,
  output c0,
  output d0,
  output e0,
  output f0,
  output g0,
  output \报警 
);

  wire \二进制转8421码电路_1_s1 , \二进制转8421码电路_1_s2 , \二进制转8421码电路_1_s4 , \二进制转8421码电路_1_s8 , \二进制转8421码电路_1_s10 ,
       \二进制转8421码电路_1_s20 , \二进制转8421码电路_1_s40 , \二进制转8421码电路_1_s80 , \报警电路_1_out_9 , \报警电路_1_out_10 ,
       \报警电路_1_out_11 , \报警电路_1_out_12 ;

  \显示电路  \u_显示电路_1  (
    .A3(\二进制转8421码电路_1_s80 ), .A2(\二进制转8421码电路_1_s40 ), .A1(\二进制转8421码电路_1_s20 ), .A0(\二进制转8421码电路_1_s10 ),
    .a(a1), .b(b1), .c(c1), .d(d1), .e(e1), .f(f1), .g(g1));
  \二进制转8421码电路  \u_二进制转8421码电路_1  (
    .S20(\二进制转8421码电路_1_s20 ), .S40(\二进制转8421码电路_1_s40 ), .S80(\二进制转8421码电路_1_s80 ),
    .S10(\二进制转8421码电路_1_s10 ), .S8(\二进制转8421码电路_1_s8 ), .S4(\二进制转8421码电路_1_s4 ), .S2(\二进制转8421码电路_1_s2 ),
    .S1(\二进制转8421码电路_1_s1 ), .D(\报警电路_1_out_9 ), .C(\报警电路_1_out_10 ), .B(\报警电路_1_out_11 ), .A(\报警电路_1_out_12 ));
  \报警电路  \u_报警电路_1  (
    .CPu(CPu), .CLR(CLR), .CPd(CPd), .out_9(\报警电路_1_out_9 ), .out_10(\报警电路_1_out_10 ),
    .out_11(\报警电路_1_out_11 ), .out_12(\报警电路_1_out_12 ), .in_4(1'b0), .in_5(1'b0), .in_6(1'b0), .in_7(1'b0),
    .in_8(1'b1), .\报警 (\报警 ));
  \显示电路  \u_显示电路_2  (
    .A3(\二进制转8421码电路_1_s8 ), .A2(\二进制转8421码电路_1_s4 ), .A1(\二进制转8421码电路_1_s2 ), .A0(\二进制转8421码电路_1_s1 ),
    .a(a0), .b(b0), .c(c0), .d(d0), .e(e0), .f(f0), .g(g0));
endmodule

module \小型门禁系统测试电路  (
  input  CPu,
  input  CLR,
  input  CPu_2
);

  wire \小型实验室门禁系统_1_a0 , \小型实验室门禁系统_1_a1 , \小型实验室门禁系统_1_b0 , \小型实验室门禁系统_1_b1 , \小型实验室门禁系统_1_c0 ,
       \小型实验室门禁系统_1_c1 , \小型实验室门禁系统_1_d0 , \小型实验室门禁系统_1_d1 , \小型实验室门禁系统_1_e0 , \小型实验室门禁系统_1_e1 ,
       \小型实验室门禁系统_1_f0 , \小型实验室门禁系统_1_f1 , \小型实验室门禁系统_1_g0 , \小型实验室门禁系统_1_g1 , \小型实验室门禁系统_1_报警 ;

  _7_Segment_Display #(.active("true")) u_7_segment_display_1 (
    .g(\小型实验室门禁系统_1_g1 ), .f(\小型实验室门禁系统_1_f1 ), .a(\小型实验室门禁系统_1_a1 ), .b(\小型实验室门禁系统_1_b1 ),
    .e(\小型实验室门禁系统_1_e1 ), .d(\小型实验室门禁系统_1_d1 ), .c(\小型实验室门禁系统_1_c1 ));  // open: dp
  \小型实验室门禁系统  \u_小型实验室门禁系统_1  (
    .CPu(CPu), .CLR(CLR), .CPd(CPu_2), .\报警 (\小型实验室门禁系统_1_报警 ), .a1(\小型实验室门禁系统_1_a1 ), .b1(\小型实验室门禁系统_1_b1 ),
    .c1(\小型实验室门禁系统_1_c1 ), .d1(\小型实验室门禁系统_1_d1 ), .e1(\小型实验室门禁系统_1_e1 ), .f1(\小型实验室门禁系统_1_f1 ),
    .g1(\小型实验室门禁系统_1_g1 ), .a0(\小型实验室门禁系统_1_a0 ), .b0(\小型实验室门禁系统_1_b0 ), .c0(\小型实验室门禁系统_1_c0 ),
    .d0(\小型实验室门禁系统_1_d0 ), .e0(\小型实验室门禁系统_1_e0 ), .f0(\小型实验室门禁系统_1_f0 ), .g0(\小型实验室门禁系统_1_g0 ));
  _7_Segment_Display #(.active("true")) u_7_segment_display_2 (
    .g(\小型实验室门禁系统_1_g0 ), .f(\小型实验室门禁系统_1_f0 ), .a(\小型实验室门禁系统_1_a0 ), .b(\小型实验室门禁系统_1_b0 ),
    .e(\小型实验室门禁系统_1_e0 ), .d(\小型实验室门禁系统_1_d0 ), .c(\小型实验室门禁系统_1_c0 ));  // open: dp
  LED #(.active("true")) led_1 (.in(\小型实验室门禁系统_1_报警 ));
endmodule
