// Logisim project 实验3.circ as structural Verilog: 6 circuits, main circuit 四位乘法器
// Mul 4 X 4
module \四位乘法器  (
  input  [3:0] a,
  input  [3:0] b,
  output [7:0] P
);

  wire [7:0] adder_1_out, adder_2_out, adder_3_out, adder_4_out, bit_extender_1_out, multiplexer_1_out,
       multiplexer_2_out, multiplexer_3_out, shifter_1_out, shifter_2_out, shifter_3_out;

  assign bit_extender_1_out = {{4{1'b0}}, b};  // Bit_Extender bit_extender_1
  Adder #(.width(8)) adder_1 (.a({8{1'b0}}), .b(bit_extender_1_out), .out(adder_1_out));  // open: cin, cout
  Shifter #(.width(8), .shift("ll")) shifter_1 (.in(bit_extender_1_out), .\dist (3'b001), .out(shifter_1_out));
  Multiplexer #(.select(1), .width(8), .disabled("Z"), .enable("false")) multiplexer_1 (
    .in0({8{1'b0}}), .in1(adder_1_out), .out(multiplexer_1_out), .sel(a[0]));
  Multiplexer #(.select(1), .width(8), .disabled("Z"), .enable("false")) multiplexer_2 (
    .in0(multiplexer_1_out), .in1(adder_2_out), .out(multiplexer_2_out), .sel(a[1]));
  Adder #(.width(8)) adder_2 (.a(multiplexer_1_out), .b(shifter_1_out), .out(adder_2_out));  // open: cin, cout
  Shifter #(.width(8), .shift("ll")) shifter_2 (.in(shifter_1_out), .\dist (3'b001), .out(shifter_2_out));
  Adder #(.width(8)) adder_3 (.a(multiplexer_2_out), .b(shifter_2_out), .out(adder_3_out));  // open: cin, cout
  Shifter #(.width(8), .shift("ll")) shifter_3 (.in(shifter_2_out), .\dist (3'b001), .out(shifter_3_out));
  Multiplexer #(.select(1), .width(8), .disabled("Z"), .enable("false")) multiplexer_3 (
    .in0(multiplexer_2_out), .in1(adder_3_out), .out(multiplexer_3_out), .sel(a[2]));
  Adder #(.width(8)) adder_4 (.a(multiplexer_3_out), .b(shifter_3_out), .out(adder_4_out));  // open: cin, cout
  Multiplexer #(.select(1), .width(8), .disabled("Z"), .enable("false")) multiplexer_4 (
    .in0(multiplexer_3_out), .in1(adder_4_out), .out(P), .sel(a[3]));
endmodule

module \四位乘法器测试电路  (
  input  [3:0] a,
  input  [3:0] b,
  output [7:0] p
);

  \四位乘法器  \u_四位乘法器_1  (.a(a), .b(b), .P(p));
endmodule

// Mul 32 X 32
module \_32X4乘法器  (
  input  [3:0] a,
  input  [31:0] b,
  output [31:0] P
);

  wire [31:0] adder_1_out, adder_2_out, adder_3_out, adder_4_out, multiplexer_1_out, multiplexer_2_out,
       multiplexer_3_out, shifter_1_out, shifter_2_out, shifter_3_out;

  Adder #(.width(32)) adder_1 (.a({32{1'b0}}), .b(b), .out(adder_1_out));  // open: cin, cout
  Shifter #(.width(32), .shift("ll")) shifter_1 (.in(b), .\dist (5'b00001), .out(shifter_1_out));
  Multiplexer #(.select(1), .width(32), .disabled("Z"), .enable("false")) multiplexer_1 (
    .in0({32{1'b0}}), .in1(adder_1_out), .out(multiplexer_1_out), .sel(a[0]));
  Multiplexer #(.select(1), .width(32), .disabled("Z"), .enable("false")) multiplexer_2 (
    .in0(multiplexer_1_out), .in1(adder_2_out), .out(multiplexer_2_out), .sel(a[1]));
  Adder #(.width(32)) adder_2 (.a(multiplexer_1_out), .b(shifter_1_out), .out(adder_2_out));  // open: cin, cout
  Shifter #(.width(32), .shift("ll")) shifter_2 (.in(shifter_1_out), .\dist (5'b00001), .out(shifter_2_out));
  Adder #(.width(32)) adder_3 (.a(multiplexer_2_out), .b(shifter_2_out), .out(adder_3_out));  // open: cin, cout
  Shifter #(.width(32), .shift("ll")) shifter_3 (.in(shifter_2_out), .\dist (5'b00001), .out(shifter_3_out));
  Multiplexer #(.select(1), .width(32), .disabled("Z"), .enable("false")) multiplexer_3 (
    .in0(multiplexer_2_out), .in1(adder_3_out), .out(multiplexer_3_out), .sel(a[2]));
  Adder #(.width(32)) adder_4 (.a(multiplexer_3_out), .b(shifter_3_out), .out(adder_4_out));  // open: cin, cout
  Multiplexer #(.select(1), .width(32), .disabled("Z"), .enable("false")) multiplexer_4 (
    .in0(multiplexer_3_out), .in1(adder_4_out), .out(P), .sel(a[3]));
endmodule

module \_32X4乘法器测试电路  (
  input  [3:0] in_1,
  input  [31:0] in_2,
  output [31:0] out_3
);

  \_32X4乘法器  \u_32x4乘法器_1  (.a(in_1), .b(in_2), .P(out_3));
endmodule

// Mul 32 X 32
module \_32X32乘法器  (
  input  [31:0] a,
  input  [31:0] b,
  output [31:0] p
);

  wire [31:0] adder_1_out, adder_2_out, adder_3_out, adder_4_out, adder_5_out, adder_6_out, \n32x4乘法器_1_p ,
       \n32x4乘法器_2_p , \n32x4乘法器_3_p , \n32x4乘法器_4_p , \n32x4乘法器_5_p , \n32x4乘法器_6_p , \n32x4乘法器_7_p ,
       \n32x4乘法器_8_p , shifter_1_out, shifter_2_out, shifter_3_out, shifter_4_out, shifter_5_out,
       shifter_6_out, shifter_7_out;

  \_32X4乘法器  \u_32x4乘法器_1  (.a(a[31:28]), .b(b), .P(\n32x4乘法器_1_p ));
  \_32X4乘法器  \u_32x4乘法器_2  (.a(a[27:24]), .b(b), .P(\n32x4乘法器_2_p ));
  \_32X4乘法器  \u_32x4乘法器_3  (.a(a[23:20]), .b(b), .P(\n32x4乘法器_3_p ));
  \_32X4乘法器  \u_32x4乘法器_4  (.a(a[19:16]), .b(b), .P(\n32x4乘法器_4_p ));
  \_32X4乘法器  \u_32x4乘法器_5  (.a(a[15:12]), .b(b), .P(\n32x4乘法器_5_p ));
  \_32X4乘法器  \u_32x4乘法器_6  (.a(a[11:8]), .b(b), .P(\n32x4乘法器_6_p ));
  \_32X4乘法器  \u_32x4乘法器_7  (.a(a[7:4]), .b(b), .P(\n32x4乘法器_7_p ));
  \_32X4乘法器  \u_32x4乘法器_8  (.a(a[3:0]), .b(b), .P(\n32x4乘法器_8_p ));
  Shifter #(.width(32), .shift("ll")) shifter_1 (.in(\n32x4乘法器_1_p ), .\dist (5'b11100), .out(shifter_1_out));
  Shifter #(.width(32), .shift("ll")) shifter_2 (.in(\n32x4乘法器_2_p ), .\dist (5'b11000), .out(shifter_2_out));
  Shifter #(.width(32), .shift("ll")) shifter_3 (.in(\n32x4乘法器_3_p ), .\dist (5'b10100), .out(shifter_3_out));
  Shifter #(.width(32), .shift("ll")) shifter_4 (.in(\n32x4乘法器_4_p ), .\dist (5'b10000), .out(shifter_4_out));
  Shifter #(.width(32), .shift("ll")) shifter_5 (.in(\n32x4乘法器_5_p ), .\dist (5'b01100), .out(shifter_5_out));
  Shifter #(.width(32), .shift("ll")) shifter_6 (.in(\n32x4乘法器_6_p ), .\dist (5'b01000), .out(shifter_6_out));
  Shifter #(.width(32), .shift("ll")) shifter_7 (.in(\n32x4乘法器_7_p ), .\dist (5'b00100), .out(shifter_7_out));
  Adder #(.width(32)) adder_1 (.a(shifter_1_out), .b(shifter_2_out), .out(adder_1_out));  // open: cin, cout
  Adder #(.width(32)) adder_2 (.a(shifter_3_out), .b(shifter_4_out), .out(adder_2_out));  // open: cin, cout
  Adder #(.width(32)) adder_3 (.a(shifter_5_out), .b(shifter_6_out), .out(adder_3_out));  // open: cin, cout
  Adder #(.width(32)) adder_4 (.a(shifter_7_out), .b(\n32x4乘法器_8_p ), .out(adder_4_out));  // open: cin, cout
  Adder #(.width(32)) adder_5 (.a(adder_1_out), .b(adder_2_out), .out(adder_5_out));  // open: cin, cout
  Adder #(.width(32)) adder_6 (.a(adder_3_out), .b(adder_4_out), .out(adder_6_out));  // open: cin, cout
  Adder #(.width(32)) adder_7 (.a(adder_5_out), .b(adder_6_out), .out(p));  // open: cin, cout
endmodule

module \_32X32乘法器测试电路  (
  input  [31:0] a,
  input  [31:0] b,
  output [31:0] out_3
);

  \_32X32乘法器  \u_32x32乘法器_1  (.a(a), .b(b), .p(out_3));
endmodule
