// Logisim project 实验4.circ as structural Verilog: 5 circuits, main circuit 四位除法器
module \四位除法器  (
  input  [3:0] n2,
  input  [3:0] d,
  output [3:0] quot,
  output [3:0] rem
);

  wire comparator_1_eq, comparator_1_gt, comparator_2_eq, comparator_2_gt, comparator_3_eq, comparator_3_gt,
       comparator_4_eq, comparator_4_gt, or_2_out, or_4_out, or_6_out, or_8_out;
  wire [3:0] multiplexer_1_out, multiplexer_2_out, multiplexer_5_out, multiplexer_6_out, or_1_out, or_3_out,
       or_5_out, or_7_out, subtractor_1_out, subtractor_2_out, subtractor_3_out, subtractor_4_out;
  wire [7:0] multiplexer_3_out, shifter_1_out, shifter_2_out, shifter_3_out, shifter_4_out;

  assign or_1_out = 4'b0001 | shifter_1_out[3:0];  // OR_Gate or_1, 4 bits wide
  Shifter #(.width(8), .shift("ll")) shifter_1 (.in({4'b0000, n2}), .\dist (3'b001), .out(shifter_1_out));
  Multiplexer #(.select(1), .width(4), .disabled("Z"), .enable("false")) multiplexer_1 (
    .in0(shifter_1_out[3:0]), .in1(or_1_out), .out(multiplexer_1_out), .sel(or_2_out));
  or or_2 (or_2_out, comparator_1_gt, comparator_1_eq);
  Comparator #(.width(4), .mode("unsigned")) comparator_1 (
    .a(shifter_1_out[7:4]), .b(d), .gt(comparator_1_gt), .eq(comparator_1_eq));  // open: lt
  Multiplexer #(.select(1), .width(4), .disabled("Z"), .enable("false")) multiplexer_2 (
    .in0(shifter_1_out[7:4]), .in1(subtractor_1_out), .out(multiplexer_2_out), .sel(or_2_out));
  Subtractor #(.width(4)) subtractor_1 (.a(shifter_1_out[7:4]), .b(d), .out(subtractor_1_out));  // open: bin, bout
  Shifter #(.width(8), .shift("ll")) shifter_2 (
    .in({multiplexer_2_out, multiplexer_1_out}), .\dist (3'b001), .out(shifter_2_out));
  assign or_3_out = 4'b0001 | shifter_2_out[3:0];  // OR_Gate or_3, 4 bits wide
  Comparator #(.width(4), .mode("unsigned")) comparator_2 (
    .a(shifter_2_out[7:4]), .b(d), .gt(comparator_2_gt), .eq(comparator_2_eq));  // open: lt
  Subtractor #(.width(4)) subtractor_2 (.a(shifter_2_out[7:4]), .b(d), .out(subtractor_2_out));  // open: bin, bout
  Multiplexer #(.select(1), .width(4), .disabled("Z"), .enable("false")) multiplexer_3 (
    .in0(shifter_2_out[3:0]), .in1(or_3_out), .out(multiplexer_3_out[3:0]), .sel(or_4_out));
  or or_4 (or_4_out, comparator_2_gt, comparator_2_eq);
  Multiplexer #(.select(1), .width(4), .disabled("Z"), .enable("false")) multiplexer_4 (
    .in0(shifter_2_out[7:4]), .in1(subtractor_2_out), .out(multiplexer_3_out[7:4]), .sel(or_4_out));
  Shifter #(.width(8), .shift("ll")) shifter_3 (.in(multiplexer_3_out), .\dist (3'b001), .out(shifter_3_out));
  assign or_5_out = 4'b0001 | shifter_3_out[3:0];  // OR_Gate or_5, 4 bits wide
  Comparator #(.width(4), .mode("unsigned")) comparator_3 (
    .a(shifter_3_out[7:4]), .b(d), .gt(comparator_3_gt), .eq(comparator_3_eq));  // open: lt
  Subtractor #(.width(4)) subtractor_3 (.a(shifter_3_out[7:4]), .b(d), .out(subtractor_3_out));  // open: bin, bout
  Multiplexer #(.select(1), .width(4), .disabled("Z"), .enable("false")) multiplexer_5 (
    .in0(shifter_3_out[3:0]), .in1(or_5_out), .out(multiplexer_5_out), .sel(or_6_out));
  or or_6 (or_6_out, comparator_3_gt, comparator_3_eq);
  Multiplexer #(.select(1), .width(4), .disabled("Z"), .enable("false")) multiplexer_6 (
    .in0(shifter_3_out[7:4]), .in1(subtractor_3_out), .out(multiplexer_6_out), .sel(or_6_out));
  Shifter #(.width(8), .shift("ll")) shifter_4 (
    .in({multiplexer_6_out, multiplexer_5_out}), .\dist (3'b001), .out(shifter_4_out));
  assign or_7_out = 4'b0001 | shifter_4_out[3:0];  // OR_Gate or_7, 4 bits wide
  Comparator #(.width(4), .mode("unsigned")) comparator_4 (
    .a(shifter_4_out[7:4]), .b(d), .gt(comparator_4_gt), .eq(comparator_4_eq));  // open: lt
  Subtractor #(.width(4)) subtractor_4 (.a(shifter_4_out[7:4]), .b(d), .out(subtractor_4_out));  // open: bin, bout
  Multiplexer #(.select(1), .width(4), .disabled("Z"), .enable("false")) multiplexer_7 (
    .in0(shifter_4_out[3:0]), .in1(or_7_out), .out(quot), .sel(or_8_out));
  or or_8 (or_8_out, comparator_4_gt, comparator_4_eq);
  Multiplexer #(.select(1), .width(4), .disabled("Z"), .enable("false")) multiplexer_8 (
    .in0(shifter_4_out[7:4]), .in1(subtractor_4_out), .out(rem), .sel(or_8_out));
endmodule

module \四位除法器测试电路  (
  input  [3:0] in_1,
  input  [3:0] in_2,
  output [3:0] out_3,
  output [3:0] out_4
);

  \四位除法器  \u_四位除法器_1  (.n2(in_1), .d(in_2), .quot(out_3), .rem(out_4));
endmodule

module _32div (
  input  [31:0] in_1,
  input  [31:0] in_2,
  input  [31:0] in_3,
  output [31:0] out_4,
  output [31:0] out_5,
  output [31:0] out_6
);

  wire bitselector_1_out, comparator_1_eq, comparator_1_gt, or_3_out;
  wire [31:0] bit_extender_1_out, or_1_out, or_2_out, shifter_1_out, shifter_2_out, subtractor_1_out;

  BitSelector #(.width(32), .group(1)) bitselector_1 (.in(in_1), .out(bitselector_1_out), .sel({5{1'b1}}));
  Shifter #(.width(32), .shift("ll")) shifter_1 (.in(in_1), .\dist (5'b00001), .out(shifter_1_out));
  assign bit_extender_1_out = {{31{1'b0}}, bitselector_1_out};  // Bit_Extender bit_extender_1
  Shifter #(.width(32), .shift("ll")) shifter_2 (.in(in_2), .\dist (5'b00001), .out(shifter_2_out));
  assign or_1_out = bit_extender_1_out | shifter_2_out;  // OR_Gate or_1, 32 bits wide
  assign or_2_out = shifter_1_out | 32'h1;  // OR_Gate or_2, 32 bits wide
  Comparator #(.width(32), .mode("unsigned")) comparator_1 (
    .a(or_1_out), .b(in_3), .gt(comparator_1_gt), .eq(comparator_1_eq));  // open: lt
  Subtractor #(.width(32)) subtractor_1 (.a(or_1_out), .b(in_3), .out(subtractor_1_out));  // open: bin, bout
  or or_3 (or_3_out, comparator_1_gt, comparator_1_eq);
  Multiplexer #(.select(1), .width(32), .disabled("Z"), .enable("false")) multiplexer_1 (
    .in0(shifter_1_out), .in1(or_2_out), .out(out_4), .sel(or_3_out));
  Multiplexer #(.select(1), .width(32), .disabled("Z"), .enable("false")) multiplexer_2 (
    .in0(or_1_out), .in1(subtractor_1_out), .out(out_5), .sel(or_3_out));

  assign out_6 = in_3;
endmodule

module \_32位除法器  (
  input  [31:0] n2,
  input  [31:0] d,
  output [31:0] quot,
  output [31:0] rem
);

  wire [31:0] n32div_1_out_4, n32div_1_out_5, n32div_1_out_6, n32div_2_out_4, n32div_2_out_5, n32div_2_out_6,
       n32div_3_out_4, n32div_3_out_5, n32div_3_out_6, n32div_4_out_4, n32div_4_out_5, n32div_4_out_6,
       n32div_5_out_4, n32div_5_out_5, n32div_5_out_6, n32div_6_out_4, n32div_6_out_5, n32div_6_out_6,
       n32div_7_out_4, n32div_7_out_5, n32div_7_out_6, n32div_8_out_4, n32div_8_out_5, n32div_8_out_6,
       n32div_9_out_4, n32div_9_out_5, n32div_9_out_6, n32div_10_out_4, n32div_10_out_5, n32div_10_out_6,
       n32div_11_out_4, n32div_11_out_5, n32div_11_out_6, n32div_12_out_4, n32div_12_out_5, n32div_12_out_6,
       n32div_13_out_4, n32div_13_out_5, n32div_13_out_6, n32div_14_out_4, n32div_14_out_5, n32div_14_out_6,
       n32div_15_out_4, n32div_15_out_5, n32div_15_out_6, n32div_16_out_4, n32div_16_out_5, n32div_16_out_6,
       n32div_17_out_4, n32div_17_out_5, n32div_17_out_6, n32div_18_out_4, n32div_18_out_5, n32div_18_out_6,
       n32div_19_out_4, n32div_19_out_5, n32div_19_out_6, n32div_20_out_4, n32div_20_out_5, n32div_20_out_6,
       n32div_21_out_4, n32div_21_out_5, n32div_21_out_6, n32div_22_out_4, n32div_22_out_5, n32div_22_out_6,
       n32div_23_out_4, n32div_23_out_5, n32div_23_out_6, n32div_24_out_4, n32div_24_out_5, n32div_24_out_6,
       n32div_26_out_4, n32div_26_out_5, n32div_26_out_6, n32div_27_out_4, n32div_27_out_5, n32div_27_out_6,
       n32div_28_out_4, n32div_28_out_5, n32div_28_out_6, n32div_29_out_4, n32div_29_out_5, n32div_29_out_6,
       n32div_30_out_4, n32div_30_out_5, n32div_30_out_6, n32div_31_out_4, n32div_31_out_5, n32div_31_out_6,
       n32div_32_out_4, n32div_32_out_5, n32div_32_out_6;

  _32div u_32div_1 (
    .in_1(n32div_3_out_4), .in_2(n32div_3_out_5), .in_3(n32div_3_out_6), .out_4(n32div_1_out_4),
    .out_5(n32div_1_out_5), .out_6(n32div_1_out_6));
  _32div u_32div_2 (
    .in_1(n2), .in_2({32{1'b0}}), .in_3(d), .out_4(n32div_2_out_4), .out_5(n32div_2_out_5),
    .out_6(n32div_2_out_6));
  _32div u_32div_3 (
    .in_1(n32div_7_out_4), .in_2(n32div_7_out_5), .in_3(n32div_7_out_6), .out_4(n32div_3_out_4),
    .out_5(n32div_3_out_5), .out_6(n32div_3_out_6));
  _32div u_32div_4 (
    .in_1(n32div_1_out_4), .in_2(n32div_1_out_5), .in_3(n32div_1_out_6), .out_4(n32div_4_out_4),
    .out_5(n32div_4_out_5), .out_6(n32div_4_out_6));
  _32div u_32div_5 (
    .in_1(n32div_2_out_4), .in_2(n32div_2_out_5), .in_3(n32div_2_out_6), .out_4(n32div_5_out_4),
    .out_5(n32div_5_out_5), .out_6(n32div_5_out_6));
  _32div u_32div_6 (
    .in_1(n32div_4_out_4), .in_2(n32div_4_out_5), .in_3(n32div_4_out_6), .out_4(n32div_6_out_4),
    .out_5(n32div_6_out_5), .out_6(n32div_6_out_6));
  _32div u_32div_7 (
    .in_1(n32div_10_out_4), .in_2(n32div_10_out_5), .in_3(n32div_10_out_6), .out_4(n32div_7_out_4),
    .out_5(n32div_7_out_5), .out_6(n32div_7_out_6));
  _32div u_32div_8 (
    .in_1(n32div_5_out_4), .in_2(n32div_5_out_5), .in_3(n32div_5_out_6), .out_4(n32div_8_out_4),
    .out_5(n32div_8_out_5), .out_6(n32div_8_out_6));
  _32div u_32div_9 (
    .in_1(n32div_6_out_4), .in_2(n32div_6_out_5), .in_3(n32div_6_out_6), .out_4(n32div_9_out_4),
    .out_5(n32div_9_out_5), .out_6(n32div_9_out_6));
  _32div u_32div_10 (
    .in_1(n32div_13_out_4), .in_2(n32div_13_out_5), .in_3(n32div_13_out_6), .out_4(n32div_10_out_4),
    .out_5(n32div_10_out_5), .out_6(n32div_10_out_6));
  _32div u_32div_11 (
    .in_1(n32div_8_out_4), .in_2(n32div_8_out_5), .in_3(n32div_8_out_6), .out_4(n32div_11_out_4),
    .out_5(n32div_11_out_5), .out_6(n32div_11_out_6));
  _32div u_32div_12 (
    .in_1(n32div_9_out_4), .in_2(n32div_9_out_5), .in_3(n32div_9_out_6), .out_4(n32div_12_out_4),
    .out_5(n32div_12_out_5), .out_6(n32div_12_out_6));
  _32div u_32div_13 (
    .in_1(n32div_15_out_4), .in_2(n32div_15_out_5), .in_3(n32div_15_out_6), .out_4(n32div_13_out_4),
    .out_5(n32div_13_out_5), .out_6(n32div_13_out_6));
  _32div u_32div_14 (
    .in_1(n32div_11_out_4), .in_2(n32div_11_out_5), .in_3(n32div_11_out_6), .out_4(n32div_14_out_4),
    .out_5(n32div_14_out_5), .out_6(n32div_14_out_6));
  _32div u_32div_15 (
    .in_1(n32div_18_out_4), .in_2(n32div_18_out_5), .in_3(n32div_18_out_6), .out_4(n32div_15_out_4),
    .out_5(n32div_15_out_5), .out_6(n32div_15_out_6));
  _32div u_32div_16 (
    .in_1(n32div_12_out_4), .in_2(n32div_12_out_5), .in_3(n32div_12_out_6), .out_4(n32div_16_out_4),
    .out_5(n32div_16_out_5), .out_6(n32div_16_out_6));
  _32div u_32div_17 (
    .in_1(n32div_14_out_4), .in_2(n32div_14_out_5), .in_3(n32div_14_out_6), .out_4(n32div_17_out_4),
    .out_5(n32div_17_out_5), .out_6(n32div_17_out_6));
  _32div u_32div_18 (
    .in_1(n32div_21_out_4), .in_2(n32div_21_out_5), .in_3(n32div_21_out_6), .out_4(n32div_18_out_4),
    .out_5(n32div_18_out_5), .out_6(n32div_18_out_6));
  _32div u_32div_19 (
    .in_1(n32div_16_out_4), .in_2(n32div_16_out_5), .in_3(n32div_16_out_6), .out_4(n32div_19_out_4),
    .out_5(n32div_19_out_5), .out_6(n32div_19_out_6));
  _32div u_32div_20 (
    .in_1(n32div_17_out_4), .in_2(n32div_17_out_5), .in_3(n32div_17_out_6), .out_4(n32div_20_out_4),
    .out_5(n32div_20_out_5), .out_6(n32div_20_out_6));
  _32div u_32div_21 (
    .in_1(n32div_24_out_4), .in_2(n32div_24_out_5), .in_3(n32div_24_out_6), .out_4(n32div_21_out_4),
    .out_5(n32div_21_out_5), .out_6(n32div_21_out_6));
  _32div u_32div_22 (
    .in_1(n32div_19_out_4), .in_2(n32div_19_out_5), .in_3(n32div_19_out_6), .out_4(n32div_22_out_4),
    .out_5(n32div_22_out_5), .out_6(n32div_22_out_6));
  _32div u_32div_23 (
    .in_1(n32div_20_out_4), .in_2(n32div_20_out_5), .in_3(n32div_20_out_6), .out_4(n32div_23_out_4),
    .out_5(n32div_23_out_5), .out_6(n32div_23_out_6));
  _32div u_32div_24 (
    .in_1(n32div_28_out_4), .in_2(n32div_28_out_5), .in_3(n32div_28_out_6), .out_4(n32div_24_out_4),
    .out_5(n32div_24_out_5), .out_6(n32div_24_out_6));
  _32div u_32div_25 (
    .in_1(n32div_29_out_4), .in_2(n32div_29_out_5), .in_3(n32div_29_out_6), .out_4(quot), .out_5(rem));  // open: out_6
  _32div u_32div_26 (
    .in_1(n32div_22_out_4), .in_2(n32div_22_out_5), .in_3(n32div_22_out_6), .out_4(n32div_26_out_4),
    .out_5(n32div_26_out_5), .out_6(n32div_26_out_6));
  _32div u_32div_27 (
    .in_1(n32div_23_out_4), .in_2(n32div_23_out_5), .in_3(n32div_23_out_6), .out_4(n32div_27_out_4),
    .out_5(n32div_27_out_5), .out_6(n32div_27_out_6));
  _32div u_32div_28 (
    .in_1(n32div_31_out_4), .in_2(n32div_31_out_5), .in_3(n32div_31_out_6), .out_4(n32div_28_out_4),
    .out_5(n32div_28_out_5), .out_6(n32div_28_out_6));
  _32div u_32div_29 (
    .in_1(n32div_32_out_4), .in_2(n32div_32_out_5), .in_3(n32div_32_out_6), .out_4(n32div_29_out_4),
    .out_5(n32div_29_out_5), .out_6(n32div_29_out_6));
  _32div u_32div_30 (
    .in_1(n32div_26_out_4), .in_2(n32div_26_out_5), .in_3(n32div_26_out_6), .out_4(n32div_30_out_4),
    .out_5(n32div_30_out_5), .out_6(n32div_30_out_6));
  _32div u_32div_31 (
    .in_1(n32div_27_out_4), .in_2(n32div_27_out_5), .in_3(n32div_27_out_6), .out_4(n32div_31_out_4),
    .out_5(n32div_31_out_5), .out_6(n32div_31_out_6));
  _32div u_32div_32 (
    .in_1(n32div_30_out_4), .in_2(n32div_30_out_5), .in_3(n32div_30_out_6), .out_4(n32div_32_out_4),
    .out_5(n32div_32_out_5), .out_6(n32div_32_out_6));
endmodule

module \_32位除法器测试电路  (
  input  [31:0] in_1,
  input  [31:0] in_2,
  output [31:0] out_3,
  output [31:0] out_4
);

  \_32位除法器  \u_32位除法器_1  (.n2(in_1), .d(in_2), .quot(out_3), .rem(out_4));
endmodule
