// Logisim project 实验5.circ as structural Verilog
module \四位二进制可逆计数器  (
  input  input_A,
  input  down_count,
  input  up_count,
  input  input_B,
  input  input_C,
  input  input_D,
  input  clear,
  input  load,
  output Qa,
  output Qb,
  output Qc,
  output Qd
);

  wire and_1_out, and_2_out, and_3_out, and_4_out, and_5_out, and_6_out, d_ff_1_qn, d_ff_2_qn, d_ff_3_qn,
       nand_1_out, nand_2_out, nand_3_out, nand_4_out, nand_5_out, nand_6_out, nand_7_out, nand_8_out,
       not_1_out, not_2_out, not_3_out, not_4_out, not_5_out, not_6_out, not_7_out, not_8_out, not_9_out,
       not_10_out, or_1_out, or_2_out, or_3_out, or_4_out, or_5_out, or_6_out, or_7_out, or_8_out;

  not not_1 (not_1_out, clear);
  not not_2 (not_2_out, load);
  nand nand_1 (nand_1_out, input_A, not_2_out, not_1_out);
  nand nand_2 (nand_2_out, input_B, not_2_out, not_1_out);
  and and_1 (and_1_out, down_count, d_ff_1_qn);
  and and_2 (and_2_out, Qa, up_count);
  nand nand_3 (nand_3_out, input_C, not_2_out, not_1_out);
  and and_3 (and_3_out, down_count, d_ff_1_qn, d_ff_2_qn);
  and and_4 (and_4_out, Qa, Qb, up_count);
  nand nand_4 (nand_4_out, input_D, not_2_out, not_1_out);
  and and_5 (and_5_out, down_count, d_ff_1_qn, d_ff_2_qn, d_ff_3_qn);
  and and_6 (and_6_out, Qa, Qb, Qc, up_count);
  or or_1 (or_1_out, and_1_out, and_2_out);
  or or_2 (or_2_out, and_3_out, and_4_out);
  or or_3 (or_3_out, down_count, up_count);
  or or_4 (or_4_out, and_5_out, and_6_out);
  nand nand_5 (nand_5_out, nand_1_out, not_2_out);
  nand nand_6 (nand_6_out, nand_2_out, not_2_out);
  nand nand_7 (nand_7_out, nand_3_out, not_2_out);
  nand nand_8 (nand_8_out, nand_4_out, not_2_out);
  or or_5 (or_5_out, ~not_1_out, ~nand_5_out);  // OR_Gate
  or or_6 (or_6_out, ~not_1_out, ~nand_6_out);  // OR_Gate
  or or_7 (or_7_out, ~not_1_out, ~nand_7_out);  // OR_Gate
  or or_8 (or_8_out, ~not_1_out, ~nand_8_out);  // OR_Gate
  not not_3 (not_3_out, nand_1_out);
  not not_4 (not_4_out, Qa);
  D_Flip_Flop #(.trigger("falling"), .Pre_Clr_Positions("ABOVE_BELOW"), .NegatePresetClear("false"), .enable("false"), .NewFFLayout("true")) d_ff_1 (
    .clk(or_3_out), .D(not_4_out), .Q(Qa), .Qn(d_ff_1_qn), .preset(not_3_out), .reset(or_5_out));
  not not_5 (not_5_out, nand_2_out);
  not not_6 (not_6_out, Qb);
  D_Flip_Flop #(.trigger("falling"), .Pre_Clr_Positions("ABOVE_BELOW"), .NegatePresetClear("false"), .enable("false"), .NewFFLayout("true")) d_ff_2 (
    .clk(or_1_out), .D(not_6_out), .Q(Qb), .Qn(d_ff_2_qn), .preset(not_5_out), .reset(or_6_out));
  not not_7 (not_7_out, nand_3_out);
  not not_8 (not_8_out, Qc);
  D_Flip_Flop #(.trigger("falling"), .Pre_Clr_Positions("ABOVE_BELOW"), .NegatePresetClear("false"), .enable("false"), .NewFFLayout("true")) d_ff_3 (
    .clk(or_2_out), .D(not_8_out), .Q(Qc), .Qn(d_ff_3_qn), .preset(not_7_out), .reset(or_7_out));
  not not_9 (not_9_out, nand_4_out);
  D_Flip_Flop #(.trigger("falling"), .Pre_Clr_Positions("ABOVE_BELOW"), .NegatePresetClear("false"), .enable("false"), .NewFFLayout("true")) d_ff_4 (
    .clk(or_4_out), .D(not_10_out), .Q(Qd), .preset(not_9_out), .reset(or_8_out));  // open: Qn
  not not_10 (not_10_out, Qd);
endmodule

module \六十进制计数器  (
  input  CLR,
  input  in_2,
  input  CPu,
  input  CPd,
  input  Adj,
  output QCC,
  output Q1D,
  output Q1C,
  output Q1B,
  output Q1A,
  output Q0D,
  output Q0C,
  output Q0B,
  output Q0A
);

  wire and_2_out, and_3_out, and_4_out, and_5_out, and_6_out, and_7_out, and_8_out, and_9_out,
       multiplexer_1_out, nand_1_out, nor_1_out, not_1_out, or_1_out, or_2_out, or_3_out, or_4_out;

  Multiplexer #(.select(1), .width(1), .disabled("Z"), .enable("false")) multiplexer_1 (
    .in0(in_2), .in1(CPu), .out(multiplexer_1_out), .sel(Adj));
  and and_1 (QCC, multiplexer_1_out, and_2_out, not_1_out, Q1C, Q1A);
  not not_1 (not_1_out, Adj);
  and and_2 (and_2_out, Q0D, Q0A);
  and and_3 (and_3_out, CPd, Adj);
  and and_4 (and_4_out, Q0D, Q0B);
  and and_5 (and_5_out, and_4_out, nand_1_out);
  nand nand_1 (nand_1_out, Q0A, Q0B, Q0C, Q0D);
  or or_1 (or_1_out, CLR, and_5_out);
  and and_6 (and_6_out, and_3_out, or_2_out);
  or or_2 (or_2_out, or_4_out, ~nor_1_out);  // OR_Gate
  \四位二进制可逆计数器  \u_四位二进制可逆计数器_1  (
    .input_A(1'b1), .down_count(and_6_out), .Qa(Q0A), .up_count(multiplexer_1_out), .input_B(1'b0), .Qb(Q0B),
    .input_C(1'b0), .Qc(Q0C), .input_D(1'b1), .clear(or_1_out), .Qd(Q0D), .load(and_7_out));
  or or_3 (or_3_out, CLR, and_8_out);
  and and_7 (and_7_out, nand_1_out, 1'b1);
  nor nor_1 (nor_1_out, Q0A, Q0B, Q0C, Q0D);
  and and_8 (and_8_out, Q1B, Q1C);
  and and_9 (and_9_out, nor_1_out, or_4_out, and_3_out);
  \四位二进制可逆计数器  \u_四位二进制可逆计数器_2  (
    .input_A(1'b0), .down_count(and_9_out), .Qa(Q1A), .up_count(and_5_out), .input_B(1'b0), .Qb(Q1B),
    .input_C(1'b0), .Qc(Q1C), .input_D(1'b0), .clear(or_3_out), .Qd(Q1D), .load(1'b1));
  or or_4 (or_4_out, Q1A, Q1B, Q1C, Q1D);
endmodule

module \六十进制计数器测试电路  (
  input  in_1,
  input  in_2,
  output out_3
);

  wire button_1_out, button_2_out, clock_1_out;
  wire [3:0] \六十进制计数器_1_q0a , \六十进制计数器_1_q1a ;

  Hex_Digit_Display hex_digit_display_1 (.value(\六十进制计数器_1_q1a ), .dp(1'b0));
  Button button_1 (.out(button_1_out));
  Button button_2 (.out(button_2_out));
  \六十进制计数器  \u_六十进制计数器_1  (
    .in_2(clock_1_out), .CPu(button_1_out), .CPd(button_2_out), .Adj(in_1), .QCC(out_3), .CLR(in_2),
    .Q0D(\六十进制计数器_1_q0a [3]), .Q0C(\六十进制计数器_1_q0a [2]), .Q0B(\六十进制计数器_1_q0a [1]), .Q0A(\六十进制计数器_1_q0a [0]),
    .Q1D(\六十进制计数器_1_q1a [3]), .Q1C(\六十进制计数器_1_q1a [2]), .Q1B(\六十进制计数器_1_q1a [1]), .Q1A(\六十进制计数器_1_q1a [0]));
  Clock #(.highDuration(1), .lowDuration(1)) clock_1 (.out(clock_1_out));
  Hex_Digit_Display hex_digit_display_2 (.value(\六十进制计数器_1_q0a ), .dp(1'b0));
endmodule

module \十二进制计数器或二十四进制的计数器电路  (
  input  Set,
  input  CPu,
  input  Adj,
  input  CPd,
  input  CLR,
  input  in_6,
  output out_7,
  output out_8,
  output out_9,
  output out_10,
  output out_11,
  output out_12,
  output out_13,
  output out_14,
  output Qcc
);

  wire and_1_out, and_2_out, and_3_out, and_4_out, and_5_out, not_1_out, not_2_out, not_3_out, or_1_out,
       or_2_out;

  Multiplexer #(.select(1), .width(1), .disabled("Z"), .enable("false")) multiplexer_1 (
    .in0(and_1_out), .in1(and_2_out), .out(Qcc), .sel(Set));
  and and_1 (and_1_out, out_10, not_1_out, out_13);
  not not_1 (not_1_out, Adj);
  and and_2 (and_2_out, not_2_out, out_9, out_13, out_14);
  not not_2 (not_2_out, Adj);
  and and_3 (and_3_out, CPu, Adj);
  \六十进制计数器  \u_六十进制计数器_1  (
    .in_2(in_6), .CPu(CPu), .CPd(CPd), .Adj(Adj), .CLR(or_1_out), .Q0D(out_11), .Q0C(out_12), .Q0B(out_13),
    .Q0A(out_14), .Q1D(out_7), .Q1C(out_8), .Q1B(out_9), .Q1A(out_10));  // open: QCC
  and and_4 (and_4_out, out_9, Set, out_12);
  or or_1 (or_1_out, and_4_out, CLR, and_5_out);
  not not_3 (not_3_out, Set);
  or or_2 (or_2_out, and_3_out, in_6);
  and and_5 (and_5_out, not_3_out, out_10, out_13, or_2_out);
endmodule

module \十二进制计数器或二十四进制的计数器测试电路  (
  input  in_1,
  input  in_2,
  input  in_3,
  output out_4
);

  wire button_1_out, button_2_out, clock_1_out;
  wire [3:0] \十二进制计数器或二十四进制的计数器电路_1_out_10 , \十二进制计数器或二十四进制的计数器电路_1_out_14 ;

  Button button_1 (.out(button_1_out));
  Button button_2 (.out(button_2_out));
  Hex_Digit_Display hex_digit_display_1 (.value(\十二进制计数器或二十四进制的计数器电路_1_out_10 ), .dp(1'b0));
  Hex_Digit_Display hex_digit_display_2 (.value(\十二进制计数器或二十四进制的计数器电路_1_out_14 ), .dp(1'b0));
  \十二进制计数器或二十四进制的计数器电路  \u_十二进制计数器或二十四进制的计数器电路_1  (
    .Qcc(out_4), .CPu(button_1_out), .Adj(in_1), .CPd(button_2_out), .CLR(in_3),
    .out_7(\十二进制计数器或二十四进制的计数器电路_1_out_10 [3]), .out_8(\十二进制计数器或二十四进制的计数器电路_1_out_10 [2]),
    .out_9(\十二进制计数器或二十四进制的计数器电路_1_out_10 [1]), .out_10(\十二进制计数器或二十四进制的计数器电路_1_out_10 [0]),
    .out_11(\十二进制计数器或二十四进制的计数器电路_1_out_14 [3]), .out_12(\十二进制计数器或二十四进制的计数器电路_1_out_14 [2]),
    .out_13(\十二进制计数器或二十四进制的计数器电路_1_out_14 [1]), .out_14(\十二进制计数器或二十四进制的计数器电路_1_out_14 [0]), .Set(in_2),
    .in_6(clock_1_out));
  Clock #(.highDuration(1), .lowDuration(1)) clock_1 (.out(clock_1_out));
endmodule

module \上下午文字显示的电路  (
  input  TT,
  input  AM_PM,
  output [4:0] out_3,
  output [4:0] out_4,
  output [4:0] out_5,
  output [4:0] out_6
);

  wire not_1_out, not_2_out, not_3_out, not_4_out, not_5_out;
  wire [4:0] controlled_buffer_1_out, controlled_buffer_3_out, controlled_buffer_5_out,
       controlled_buffer_7_out;

  assign controlled_buffer_1_out = not_1_out ? 5'b00001 : 5'bz;  // Controlled_Buffer controlled_buffer_1
  not not_1 (not_1_out, AM_PM);
  assign controlled_buffer_1_out = not_2_out ? 5'b10000 : 5'bz;  // Controlled_Buffer controlled_buffer_2
  not not_2 (not_2_out, not_1_out);
  assign controlled_buffer_3_out = not_1_out ? {5{1'b1}} : 5'bz;  // Controlled_Buffer controlled_buffer_3
  not not_3 (not_3_out, not_1_out);
  assign controlled_buffer_3_out = not_3_out ? {5{1'b1}} : 5'bz;  // Controlled_Buffer controlled_buffer_4
  assign controlled_buffer_5_out = not_1_out ? 5'b00101 : 5'bz;  // Controlled_Buffer controlled_buffer_5
  not not_4 (not_4_out, not_1_out);
  assign controlled_buffer_5_out = not_4_out ? 5'b10100 : 5'bz;  // Controlled_Buffer controlled_buffer_6
  assign controlled_buffer_7_out = not_1_out ? 5'b00001 : 5'bz;  // Controlled_Buffer controlled_buffer_7
  not not_5 (not_5_out, not_1_out);
  assign controlled_buffer_7_out = not_5_out ? 5'b10000 : 5'bz;  // Controlled_Buffer controlled_buffer_8
  assign out_4 = TT ? controlled_buffer_3_out : 5'bz;  // Controlled_Buffer controlled_buffer_9
  assign out_3 = TT ? controlled_buffer_1_out : 5'bz;  // Controlled_Buffer controlled_buffer_10
  assign out_5 = TT ? controlled_buffer_5_out : 5'bz;  // Controlled_Buffer controlled_buffer_11
  assign out_6 = TT ? controlled_buffer_7_out : 5'bz;  // Controlled_Buffer controlled_buffer_12
endmodule

module \上下午文字显示测试电路  (
  input  in_1,
  input  in_2
);

  wire [4:0] \上下午文字显示的电路_1_out_3 , \上下午文字显示的电路_1_out_4 , \上下午文字显示的电路_1_out_5 , \上下午文字显示的电路_1_out_6 ;

  \上下午文字显示的电路  \u_上下午文字显示的电路_1  (
    .TT(in_2), .out_3(\上下午文字显示的电路_1_out_3 ), .out_4(\上下午文字显示的电路_1_out_4 ), .out_5(\上下午文字显示的电路_1_out_5 ),
    .out_6(\上下午文字显示的电路_1_out_6 ), .AM_PM(in_1));
  DotMatrix #(.inputtype("column"), .matrixcols(4), .matrixrows(5), .persist(0), .dotshape("square")) dotmatrix_1 (
    .col0(\上下午文字显示的电路_1_out_3 ), .col1(\上下午文字显示的电路_1_out_4 ), .col2(\上下午文字显示的电路_1_out_5 ),
    .col3(\上下午文字显示的电路_1_out_6 ));
endmodule

module \电子钟整点报时电路  (
  input  in_1,
  input  in_2,
  input  in_3,
  input  in_4,
  input  in_5,
  input  in_6,
  output out_7
);

  and and_1 (out_7, in_1, in_2, in_3, in_4, in_5, in_6);
endmodule

module \电子钟整点报时电路测试电路  (
  input  in_1,
  input  in_2,
  input  in_3,
  output out_4,
  output out_5,
  output out_6,
  output out_7,
  output out_8,
  output out_9,
  output out_10,
  output out_11,
  output out_12,
  output out_13,
  output out_14,
  output out_15,
  output out_16,
  output out_17,
  output out_18,
  output out_19,
  output out_20
);

  wire button_1_out, button_2_out, button_3_out, button_4_out, clock_1_out, \六十进制计数器_1_qcc ,
       \电子钟整点报时电路_1_out_7 ;

  Button button_1 (.out(button_1_out));
  Button button_2 (.out(button_2_out));
  \六十进制计数器  \u_六十进制计数器_1  (
    .in_2(clock_1_out), .CPu(button_1_out), .CPd(button_2_out), .Adj(in_1), .QCC(\六十进制计数器_1_qcc ),
    .CLR(in_3), .Q0D(out_8), .Q0C(out_9), .Q0B(out_10), .Q0A(out_11), .Q1D(out_4), .Q1C(out_5), .Q1B(out_6),
    .Q1A(out_7));
  Clock #(.highDuration(1), .lowDuration(1)) clock_1 (.out(clock_1_out));
  \电子钟整点报时电路  \u_电子钟整点报时电路_1  (
    .out_7(\电子钟整点报时电路_1_out_7 ), .in_1(out_13), .in_2(out_15), .in_3(out_16), .in_4(out_19), .in_5(out_5),
    .in_6(out_7));
  LED #(.active("true")) led_1 (.in(\电子钟整点报时电路_1_out_7 ));
  Button button_3 (.out(button_3_out));
  Button button_4 (.out(button_4_out));
  \六十进制计数器  \u_六十进制计数器_2  (
    .in_2(\六十进制计数器_1_qcc ), .CPu(button_3_out), .CPd(button_4_out), .Adj(in_2), .QCC(out_20), .CLR(in_3),
    .Q0D(out_16), .Q0C(out_17), .Q0B(out_18), .Q0A(out_19), .Q1D(out_12), .Q1C(out_13), .Q1B(out_14),
    .Q1A(out_15));
endmodule

module \秒脉冲产生电路  (
  input  in_1,
  output out_2
);

  wire and_2_out, \四位二进制可逆计数器_1_qa , \四位二进制可逆计数器_1_qb , \四位二进制可逆计数器_1_qc ;

  and and_1 (out_2, in_1, and_2_out);
  and and_2 (and_2_out, \四位二进制可逆计数器_1_qa , \四位二进制可逆计数器_1_qb );
  \四位二进制可逆计数器  \u_四位二进制可逆计数器_1  (
    .input_A(1'b0), .down_count(1'b0), .Qa(\四位二进制可逆计数器_1_qa ), .up_count(in_1), .input_B(1'b0),
    .Qb(\四位二进制可逆计数器_1_qb ), .input_C(1'b0), .Qc(\四位二进制可逆计数器_1_qc ), .input_D(1'b0),
    .clear(\四位二进制可逆计数器_1_qc ), .load(1'b1));  // open: Qd
endmodule

module \多功能数字钟  (
  input  in_1,
  input  CPu,
  input  Adj0,
  input  CPd,
  input  CLR,
  input  Adj1,
  input  in_7,
  output [3:0] out_8,
  output [3:0] out_9,
  output out_10,
  output [3:0] out_11,
  output [3:0] out_12,
  output [3:0] out_13,
  output [3:0] out_14,
  output [4:0] out_15,
  output [4:0] out_16,
  output [4:0] out_17,
  output [4:0] out_18
);

  wire and_1_out, and_2_out, and_3_out, j_k_ff_1_q, not_1_out, not_2_out, \六十进制计数器_1_qcc , \六十进制计数器_2_qcc ,
       \秒脉冲产生电路_1_out_2 ;

  \六十进制计数器  \u_六十进制计数器_1  (
    .in_2(\秒脉冲产生电路_1_out_2 ), .CPu(1'b0), .CPd(1'b0), .Adj(Adj0), .QCC(\六十进制计数器_1_qcc ), .CLR(CLR),
    .Q0D(out_14[3]), .Q0C(out_14[2]), .Q0B(out_14[1]), .Q0A(out_14[0]), .Q1D(out_13[3]), .Q1C(out_13[2]),
    .Q1B(out_13[1]), .Q1A(out_13[0]));
  \秒脉冲产生电路  \u_秒脉冲产生电路_1  (.in_1(in_7), .out_2(\秒脉冲产生电路_1_out_2 ));
  \电子钟整点报时电路  \u_电子钟整点报时电路_1  (
    .out_7(out_10), .in_1(out_11[2]), .in_2(out_11[0]), .in_3(out_12[3]), .in_4(out_12[0]), .in_5(out_13[2]),
    .in_6(out_13[0]));
  and and_1 (and_1_out, Adj0, Adj1);
  \六十进制计数器  \u_六十进制计数器_2  (
    .in_2(\六十进制计数器_1_qcc ), .CPu(CPu), .CPd(CPd), .Adj(and_1_out), .QCC(\六十进制计数器_2_qcc ), .CLR(CLR),
    .Q0D(out_12[3]), .Q0C(out_12[2]), .Q0B(out_12[1]), .Q0A(out_12[0]), .Q1D(out_11[3]), .Q1C(out_11[2]),
    .Q1B(out_11[1]), .Q1A(out_11[0]));
  and and_2 (and_2_out, Adj0, not_1_out);
  not not_1 (not_1_out, Adj1);
  \十二进制计数器或二十四进制的计数器电路  \u_十二进制计数器或二十四进制的计数器电路_1  (
    .CPu(CPu), .Adj(and_2_out), .CPd(CPd), .CLR(CLR), .out_7(out_8[3]), .out_8(out_8[2]), .out_9(out_8[1]),
    .out_10(out_8[0]), .out_11(out_9[3]), .out_12(out_9[2]), .out_13(out_9[1]), .out_14(out_9[0]),
    .Set(in_1), .in_6(\六十进制计数器_2_qcc ));  // open: Qcc
  \上下午文字显示的电路  \u_上下午文字显示的电路_1  (
    .TT(not_2_out), .out_3(out_15), .out_4(out_16), .out_5(out_17), .out_6(out_18), .AM_PM(j_k_ff_1_q));
  J_K_Flip_Flop #(.trigger("rising"), .Pre_Clr_Positions("ABOVE_BELOW"), .NegatePresetClear("false"), .enable("false"), .NewFFLayout("true")) j_k_ff_1 (
    .J(1'b1), .clk(and_3_out), .K(1'b1), .Q(j_k_ff_1_q), .preset(1'b0), .reset(1'b0));  // open: Qn
  not not_2 (not_2_out, in_1);
  and and_3 (and_3_out, out_9[1], out_8[0]);
endmodule

module \多功能数字钟测试电路  (
  input  in_1,
  input  in_2,
  input  in_3,
  input  in_4
);

  wire button_1_out, button_2_out, clock_1_out, \多功能数字钟_1_out_10 ;
  wire [3:0] \多功能数字钟_1_out_8 , \多功能数字钟_1_out_9 , \多功能数字钟_1_out_11 , \多功能数字钟_1_out_12 , \多功能数字钟_1_out_13 ,
       \多功能数字钟_1_out_14 ;
  wire [4:0] \多功能数字钟_1_out_15 , \多功能数字钟_1_out_16 , \多功能数字钟_1_out_17 , \多功能数字钟_1_out_18 ;

  DotMatrix #(.inputtype("column"), .matrixcols(4), .matrixrows(5), .persist(0), .dotshape("square")) dotmatrix_1 (
    .col0(\多功能数字钟_1_out_15 ), .col1(\多功能数字钟_1_out_16 ), .col2(\多功能数字钟_1_out_17 ), .col3(\多功能数字钟_1_out_18 ));
  Hex_Digit_Display hex_digit_display_1 (.value(\多功能数字钟_1_out_8 ), .dp(1'b0));
  Clock #(.highDuration(1), .lowDuration(1)) clock_1 (.out(clock_1_out));
  Hex_Digit_Display hex_digit_display_2 (.value(\多功能数字钟_1_out_9 ), .dp(1'b0));
  \多功能数字钟  \u_多功能数字钟_1  (
    .CPu(button_2_out), .Adj0(in_1), .CPd(button_1_out), .in_1(in_3), .CLR(in_4), .out_13(\多功能数字钟_1_out_13 ),
    .out_14(\多功能数字钟_1_out_14 ), .out_10(\多功能数字钟_1_out_10 ), .out_11(\多功能数字钟_1_out_11 ),
    .out_12(\多功能数字钟_1_out_12 ), .out_8(\多功能数字钟_1_out_8 ), .out_15(\多功能数字钟_1_out_15 ),
    .out_9(\多功能数字钟_1_out_9 ), .out_16(\多功能数字钟_1_out_16 ), .out_17(\多功能数字钟_1_out_17 ),
    .out_18(\多功能数字钟_1_out_18 ), .Adj1(in_2), .in_7(clock_1_out));
  Button button_1 (.out(button_1_out));
  Button button_2 (.out(button_2_out));
  Hex_Digit_Display hex_digit_display_3 (.value(\多功能数字钟_1_out_12 ), .dp(1'b0));
  Hex_Digit_Display hex_digit_display_4 (.value(\多功能数字钟_1_out_11 ), .dp(1'b0));
  Hex_Digit_Display hex_digit_display_5 (.value(\多功能数字钟_1_out_14 ), .dp(1'b0));
  Hex_Digit_Display hex_digit_display_6 (.value(\多功能数字钟_1_out_13 ), .dp(1'b0));
  LED #(.active("true")) led_1 (.in(\多功能数字钟_1_out_10 ));
endmodule
