// Logisim project 实验6.circ as structural Verilog: 7 circuits, main circuit sqrX
module sqrX (
  input  [31:0] a,
  input  [31:0] b,
  input  [31:0] c,
  input  [31:0] d,
  output [31:0] a_prime,
  output [31:0] b_prime,
  output [31:0] c_prime,
  output [31:0] d_prime
);

  wire [31:0] multiplier_1_out, multiplier_2_out, multiplier_3_out, multiplier_4_out, multiplier_5_out,
       multiplier_6_out, multiplier_7_out;

  Multiplier #(.width(32)) multiplier_1 (.a(a), .b(a), .out(multiplier_1_out));  // open: cin, cout
  Multiplier #(.width(32)) multiplier_2 (.a(a), .b(b), .out(multiplier_2_out));  // open: cin, cout
  Multiplier #(.width(32)) multiplier_3 (.a(a), .b(c), .out(multiplier_3_out));  // open: cin, cout
  Multiplier #(.width(32)) multiplier_4 (.a(b), .b(c), .out(multiplier_4_out));  // open: cin, cout
  Multiplier #(.width(32)) multiplier_5 (.a(b), .b(d), .out(multiplier_5_out));  // open: cin, cout
  Multiplier #(.width(32)) multiplier_6 (.a(c), .b(d), .out(multiplier_6_out));  // open: cin, cout
  Multiplier #(.width(32)) multiplier_7 (.a(d), .b(d), .out(multiplier_7_out));  // open: cin, cout
  Adder #(.width(32)) adder_1 (.a(multiplier_1_out), .b(multiplier_4_out), .out(a_prime));  // open: cin, cout
  Adder #(.width(32)) adder_2 (.a(multiplier_2_out), .b(multiplier_5_out), .out(b_prime));  // open: cin, cout
  Adder #(.width(32)) adder_3 (.a(multiplier_3_out), .b(multiplier_6_out), .out(c_prime));  // open: cin, cout
  Adder #(.width(32)) adder_4 (.a(multiplier_4_out), .b(multiplier_7_out), .out(d_prime));  // open: cin, cout
endmodule

module sqrX_A (
  input  [31:0] a,
  input  [31:0] b,
  input  [31:0] c,
  input  [31:0] d,
  output [31:0] a_prime_prime,
  output [31:0] b_prime_prime,
  output [31:0] c_prime_prime,
  output [31:0] d_prime_prime
);

  wire [31:0] adder_2_out, adder_4_out, multiplier_1_out, multiplier_2_out, multiplier_3_out,
       multiplier_4_out, multiplier_5_out, multiplier_6_out, multiplier_7_out;

  Multiplier #(.width(32)) multiplier_1 (.a(a), .b(b), .out(multiplier_1_out));  // open: cin, cout
  Multiplier #(.width(32)) multiplier_2 (.a(b), .b(d), .out(multiplier_2_out));  // open: cin, cout
  Multiplier #(.width(32)) multiplier_3 (.a(a), .b(a), .out(multiplier_3_out));  // open: cin, cout
  Multiplier #(.width(32)) multiplier_4 (.a(b), .b(c), .out(multiplier_4_out));  // open: cin, cout
  Multiplier #(.width(32)) multiplier_5 (.a(d), .b(d), .out(multiplier_5_out));  // open: cin, cout
  Multiplier #(.width(32)) multiplier_6 (.a(a), .b(c), .out(multiplier_6_out));  // open: cin, cout
  Multiplier #(.width(32)) multiplier_7 (.a(c), .b(d), .out(multiplier_7_out));  // open: cin, cout
  Adder #(.width(32)) adder_1 (.a(multiplier_1_out), .b(multiplier_2_out), .out(a_prime_prime));  // open: cin, cout
  Adder #(.width(32)) adder_2 (.a(multiplier_3_out), .b(multiplier_4_out), .out(adder_2_out));  // open: cin, cout
  Adder #(.width(32)) adder_3 (.a(multiplier_4_out), .b(multiplier_5_out), .out(c_prime_prime));  // open: cin, cout
  Adder #(.width(32)) adder_4 (.a(multiplier_6_out), .b(multiplier_7_out), .out(adder_4_out));  // open: cin, cout
  Adder #(.width(32)) adder_5 (.a(a_prime_prime), .b(adder_2_out), .out(b_prime_prime));  // open: cin, cout
  Adder #(.width(32)) adder_6 (.a(c_prime_prime), .b(adder_4_out), .out(d_prime_prime));  // open: cin, cout
endmodule

module \Fibonacci数显示模块  (
  input  [31:0] in_1,
  output [3:0] out_2,
  output [3:0] out_3,
  output [3:0] out_4,
  output [3:0] out_5,
  output [3:0] out_6,
  output [3:0] out_7,
  output [3:0] out_8,
  output [3:0] out_9,
  output [3:0] out_10,
  output [3:0] out_11
);

  wire [31:0] divider_1_rem, divider_2_rem, divider_3_rem, divider_4_rem, divider_5_rem, divider_6_rem,
       divider_7_rem, divider_8_rem;
  wire [31:4] divider_1_out, divider_2_out, divider_3_out, divider_4_out, divider_5_out, divider_6_out,
       divider_7_out, divider_8_out, divider_9_out, divider_9_rem;

  Divider #(.width(32)) divider_1 (
    .a(in_1), .b(32'h3b9aca00), .out({divider_1_out, out_2}), .rem(divider_1_rem));  // open: upper
  Divider #(.width(32)) divider_2 (
    .a(divider_1_rem), .b(32'h5f5e100), .out({divider_2_out, out_3}), .rem(divider_2_rem));  // open: upper
  Divider #(.width(32)) divider_3 (
    .a(divider_2_rem), .b(32'h989680), .out({divider_3_out, out_4}), .rem(divider_3_rem));  // open: upper
  Divider #(.width(32)) divider_4 (
    .a(divider_3_rem), .b(32'hf4240), .out({divider_4_out, out_5}), .rem(divider_4_rem));  // open: upper
  Divider #(.width(32)) divider_5 (
    .a(divider_4_rem), .b(32'h186a0), .out({divider_5_out, out_6}), .rem(divider_5_rem));  // open: upper
  Divider #(.width(32)) divider_6 (
    .a(divider_5_rem), .b(32'h2710), .out({divider_6_out, out_7}), .rem(divider_6_rem));  // open: upper
  Divider #(.width(32)) divider_7 (
    .a(divider_6_rem), .b(32'h3e8), .out({divider_7_out, out_8}), .rem(divider_7_rem));  // open: upper
  Divider #(.width(32)) divider_8 (
    .a(divider_7_rem), .b(32'h64), .out({divider_8_out, out_9}), .rem(divider_8_rem));  // open: upper
  Divider #(.width(32)) divider_9 (
    .a(divider_8_rem), .b(32'ha), .out({divider_9_out, out_10}), .rem({divider_9_rem, out_11}));  // open: upper
endmodule

module \斐波那契_Fibonacci_数列计算器  (
  input  [5:0] in_1,
  input  in_2,
  input  in_3,
  output [3:0] out_4,
  output [3:0] out_5,
  output [3:0] out_6,
  output [3:0] out_7,
  output [3:0] out_8,
  output [3:0] out_9,
  output [3:0] out_10,
  output [3:0] out_11,
  output [3:0] out_12,
  output [3:0] out_13
);

  wire \控制器controller_1_clk , \控制器controller_1_n_i_1 , \控制器controller_1_out_7 , \控制器controller_1_start ;
  wire [31:0] \矩阵快速幂算法迭代fibo_1_out_5 ;

  \控制器Controller  \u_控制器controller_1  (
    .N(in_1), .CLOCK(in_3), .clear(in_2), .n_i_1(\控制器controller_1_n_i_1 ), .clk(\控制器controller_1_clk ),
    .start(\控制器controller_1_start ), .out_7(\控制器controller_1_out_7 ));
  \矩阵快速幂算法迭代Fibo  \u_矩阵快速幂算法迭代fibo_1  (
    .start(\控制器controller_1_start ), .n_i_1(\控制器controller_1_n_i_1 ), .clr(\控制器controller_1_out_7 ),
    .clk(\控制器controller_1_clk ), .out_5(\矩阵快速幂算法迭代fibo_1_out_5 ));
  \Fibonacci数显示模块  \fibonacci数显示模块_1  (
    .in_1(\矩阵快速幂算法迭代fibo_1_out_5 ), .out_2(out_4), .out_3(out_5), .out_4(out_6), .out_5(out_7),
    .out_6(out_8), .out_7(out_9), .out_8(out_10), .out_9(out_11), .out_10(out_12), .out_11(out_13));
endmodule

module \斐波那契_Fibonacci_数列计算器验证电路  (
  input  [5:0] in_1,
  input  in_2,
  input  in_3
);

  wire \控制器controller_1_clk , \控制器controller_1_n_i_1 , \控制器controller_1_out_7 , \控制器controller_1_start ;
  wire [3:0] \fibonacci数显示模块_1_out_2 , \fibonacci数显示模块_1_out_3 , \fibonacci数显示模块_1_out_4 ,
       \fibonacci数显示模块_1_out_5 , \fibonacci数显示模块_1_out_6 , \fibonacci数显示模块_1_out_7 ,
       \fibonacci数显示模块_1_out_8 , \fibonacci数显示模块_1_out_9 , \fibonacci数显示模块_1_out_10 ,
       \fibonacci数显示模块_1_out_11 ;
  wire [31:0] \矩阵快速幂算法迭代fibo_1_out_5 ;

  \控制器Controller  \u_控制器controller_1  (
    .N(in_1), .CLOCK(in_3), .clear(in_2), .n_i_1(\控制器controller_1_n_i_1 ), .clk(\控制器controller_1_clk ),
    .start(\控制器controller_1_start ), .out_7(\控制器controller_1_out_7 ));
  \矩阵快速幂算法迭代Fibo  \u_矩阵快速幂算法迭代fibo_1  (
    .start(\控制器controller_1_start ), .n_i_1(\控制器controller_1_n_i_1 ), .clr(\控制器controller_1_out_7 ),
    .clk(\控制器controller_1_clk ), .out_5(\矩阵快速幂算法迭代fibo_1_out_5 ));
  Hex_Digit_Display hex_digit_display_1 (.value(\fibonacci数显示模块_1_out_2 ));  // open: dp
  \Fibonacci数显示模块  \fibonacci数显示模块_1  (
    .in_1(\矩阵快速幂算法迭代fibo_1_out_5 ), .out_2(\fibonacci数显示模块_1_out_2 ), .out_3(\fibonacci数显示模块_1_out_3 ),
    .out_4(\fibonacci数显示模块_1_out_4 ), .out_5(\fibonacci数显示模块_1_out_5 ), .out_6(\fibonacci数显示模块_1_out_6 ),
    .out_7(\fibonacci数显示模块_1_out_7 ), .out_8(\fibonacci数显示模块_1_out_8 ), .out_9(\fibonacci数显示模块_1_out_9 ),
    .out_10(\fibonacci数显示模块_1_out_10 ), .out_11(\fibonacci数显示模块_1_out_11 ));
  Hex_Digit_Display hex_digit_display_2 (.value(\fibonacci数显示模块_1_out_3 ));  // open: dp
  Hex_Digit_Display hex_digit_display_3 (.value(\fibonacci数显示模块_1_out_4 ));  // open: dp
  Hex_Digit_Display hex_digit_display_4 (.value(\fibonacci数显示模块_1_out_5 ));  // open: dp
  Hex_Digit_Display hex_digit_display_5 (.value(\fibonacci数显示模块_1_out_6 ));  // open: dp
  Hex_Digit_Display hex_digit_display_6 (.value(\fibonacci数显示模块_1_out_8 ));  // open: dp
  Hex_Digit_Display hex_digit_display_7 (.value(\fibonacci数显示模块_1_out_7 ));  // open: dp
  Hex_Digit_Display hex_digit_display_8 (.value(\fibonacci数显示模块_1_out_9 ));  // open: dp
  Hex_Digit_Display hex_digit_display_9 (.value(\fibonacci数显示模块_1_out_10 ));  // open: dp
  Hex_Digit_Display hex_digit_display_10 (.value(\fibonacci数显示模块_1_out_11 ));  // open: dp
endmodule

module \矩阵快速幂算法迭代Fibo  (
  input  start,
  input  n_i_1,
  input  clr,
  input  clk,
  output [31:0] out_5
);

  wire and_1_out, not_1_out;
  wire [31:0] multiplexer_1_out, multiplexer_2_out, multiplexer_3_out, multiplexer_4_out, multiplexer_5_out,
       multiplexer_6_out, multiplexer_7_out, multiplexer_8_out, register_1_q, register_3_q, register_4_q,
       sqrx_1_a_prime, sqrx_1_b_prime, sqrx_1_c_prime, sqrx_1_d_prime, sqrx_a_1_a_prime_prime,
       sqrx_a_1_b_prime_prime, sqrx_a_1_c_prime_prime, sqrx_a_1_d_prime_prime;

  and and_1 (and_1_out, start, not_1_out);
  not not_1 (not_1_out, clr);
  Multiplexer #(.select(1), .width(32), .disabled("Z"), .enable("false")) multiplexer_1 (
    .in0({32{1'b0}}), .in1(multiplexer_5_out), .out(multiplexer_1_out), .sel(and_1_out));
  Multiplexer #(.select(1), .width(32), .disabled("Z"), .enable("false")) multiplexer_2 (
    .in0(32'h1), .in1(multiplexer_6_out), .out(multiplexer_2_out), .sel(and_1_out));
  Multiplexer #(.select(1), .width(32), .disabled("Z"), .enable("false")) multiplexer_3 (
    .in0(32'h1), .in1(multiplexer_7_out), .out(multiplexer_3_out), .sel(and_1_out));
  Multiplexer #(.select(1), .width(32), .disabled("Z"), .enable("false")) multiplexer_4 (
    .in0(32'h1), .in1(multiplexer_8_out), .out(multiplexer_4_out), .sel(and_1_out));
  Register #(.width(32), .trigger("rising"), .Select("low")) register_1 (
    .D(multiplexer_1_out), .en(1'b1), .Q(register_1_q), .clk(clk), .clr(clr));
  Register #(.width(32), .trigger("rising"), .Select("low")) register_2 (
    .D(multiplexer_2_out), .en(1'b1), .Q(out_5), .clk(clk), .clr(clr));
  Register #(.width(32), .trigger("rising"), .Select("low")) register_3 (
    .D(multiplexer_3_out), .en(1'b1), .Q(register_3_q), .clk(clk), .clr(clr));
  Register #(.width(32), .trigger("rising"), .Select("low")) register_4 (
    .D(multiplexer_4_out), .en(1'b1), .Q(register_4_q), .clk(clk), .clr(clr));
  sqrX sqrx_1 (
    .a(register_1_q), .b(out_5), .c(register_3_q), .d(register_4_q), .a_prime(sqrx_1_a_prime),
    .b_prime(sqrx_1_b_prime), .c_prime(sqrx_1_c_prime), .d_prime(sqrx_1_d_prime));
  sqrX_A sqrx_a_1 (
    .a(register_1_q), .b(out_5), .c(register_3_q), .d(register_4_q), .b_prime_prime(sqrx_a_1_b_prime_prime),
    .c_prime_prime(sqrx_a_1_c_prime_prime), .d_prime_prime(sqrx_a_1_d_prime_prime),
    .a_prime_prime(sqrx_a_1_a_prime_prime));
  Multiplexer #(.select(1), .width(32), .disabled("Z"), .enable("false")) multiplexer_5 (
    .in0(sqrx_1_a_prime), .in1(sqrx_a_1_a_prime_prime), .out(multiplexer_5_out), .sel(n_i_1));
  Multiplexer #(.select(1), .width(32), .disabled("Z"), .enable("false")) multiplexer_6 (
    .in0(sqrx_1_b_prime), .in1(sqrx_a_1_b_prime_prime), .out(multiplexer_6_out), .sel(n_i_1));
  Multiplexer #(.select(1), .width(32), .disabled("Z"), .enable("false")) multiplexer_7 (
    .in0(sqrx_1_c_prime), .in1(sqrx_a_1_c_prime_prime), .out(multiplexer_7_out), .sel(n_i_1));
  Multiplexer #(.select(1), .width(32), .disabled("Z"), .enable("false")) multiplexer_8 (
    .in0(sqrx_1_d_prime), .in1(sqrx_a_1_d_prime_prime), .out(multiplexer_8_out), .sel(n_i_1));
endmodule

module \控制器Controller  (
  input  [5:0] N,
  input  CLOCK,
  input  clear,
  output n_i_1,
  output clk,
  output start,
  output out_7
);

  wire comparator_1_lt, not_1_out, or_1_out, or_2_out;
  wire [7:0] counter_1_q;

  Counter #(.width(8), .max('hff), .ongoal("wrap"), .trigger("rising"), .behavior("new")) counter_1 (
    .D(8'h1), .Q(counter_1_q), .clk(CLOCK), .clr(clear));  // open: load, count, carry, preset, down
  or or_1 (or_1_out, CLOCK, clear);
  Comparator #(.width(8), .mode("twosComplement")) comparator_1 (
    .a(counter_1_q), .b(8'h6), .lt(comparator_1_lt));  // open: gt, eq
  Shift_Register #(.width(1), .length(6), .parallel("true"), .trigger("rising")) shift_register_1 (
    .shift(not_1_out), .in(1'b0), .clk(or_1_out), .out(n_i_1), .load(clear), .d0(N[0]), .d1(N[1]), .d2(N[2]),
    .d3(N[3]), .d4(N[4]), .d5(N[5]));  // open: clr, q0, q1, q2, q3, q4, q5
  not not_1 (not_1_out, clear);
  or or_2 (or_2_out, n_i_1, start);
  and and_1 (clk, comparator_1_lt, CLOCK);
  D_Flip_Flop #(.trigger("rising"), .Pre_Clr_Positions("ABOVE_BELOW"), .NegatePresetClear("false"), .enable("false"), .NewFFLayout("true")) d_ff_1 (
    .clk(CLOCK), .D(or_2_out), .Q(start), .reset(clear));  // open: Qn, preset

  assign out_7 = clear;
endmodule
